// Logisim project 01010101示波器.circ as structural Verilog: 1 circuit, main circuit main
module main (
  output out_1
);

  wire and_1_out, and_2_out, clock_1_out, decoder_1_out1, decoder_1_out3, decoder_1_out5, decoder_1_out7;
  wire [2:0] digital_oscilloscope_1_p3;

  Clock #(.highDuration(1), .lowDuration(1)) clock_1 (.out(clock_1_out));
  // Digital_Oscilloscope #(.nState(18), .frontlines("rising"), .showclock("true")) digital_oscilloscope_1: pin names not known; wires that end beside it: clock_1_out, out_1, digital_oscilloscope_1_p3[0], digital_oscilloscope_1_p3[1], digital_oscilloscope_1_p3[2]
  and and_1 (and_1_out, digital_oscilloscope_1_p3[1], digital_oscilloscope_1_p3[0]);
  J_K_Flip_Flop #(.trigger("rising"), .Pre_Clr_Positions("ABOVE_BELOW"), .NegatePresetClear("false"), .enable("false"), .NewFFLayout("true")) j_k_ff_1 (
    .J(and_1_out), .clk(clock_1_out), .K(and_1_out), .Q(digital_oscilloscope_1_p3[2]));  // open: Qn, preset, reset
  J_K_Flip_Flop #(.trigger("rising"), .Pre_Clr_Positions("ABOVE_BELOW"), .NegatePresetClear("false"), .enable("false"), .NewFFLayout("true")) j_k_ff_2 (
    .J(digital_oscilloscope_1_p3[0]), .clk(clock_1_out), .K(digital_oscilloscope_1_p3[0]),
    .Q(digital_oscilloscope_1_p3[1]));  // open: Qn, preset, reset
  J_K_Flip_Flop #(.trigger("rising"), .Pre_Clr_Positions("ABOVE_BELOW"), .NegatePresetClear("false"), .enable("false"), .NewFFLayout("true")) j_k_ff_3 (
    .J(1'b1), .clk(clock_1_out), .K(1'b1), .Q(digital_oscilloscope_1_p3[0]));  // open: Qn, preset, reset
  and and_2 (and_2_out, digital_oscilloscope_1_p3[2], digital_oscilloscope_1_p3[1], digital_oscilloscope_1_p3[0]);
  LED #(.active("true")) led_1 (.in(and_2_out));
  Decoder #(.select(3), .tristate("false"), .disabled("Z"), .enable("false")) decoder_1 (
    .out1(decoder_1_out1), .out3(decoder_1_out3), .out5(decoder_1_out5), .out7(decoder_1_out7),
    .sel(digital_oscilloscope_1_p3));  // open: out0, out2, out4, out6
  or or_1 (out_1, decoder_1_out1, decoder_1_out3, decoder_1_out5, decoder_1_out7);

  // Notes on the sheet:
  //   FF3
  //   FF2
  //   FF1
  //   Q1
  //   Q2
  //   Q3
  //   序列发生端
endmodule
