// Logisim project 100000000示波器.circ as structural Verilog: 1 circuit, main circuit main
module main (
  output out_1
);

  wire and_1_out, and_2_out, clock_1_out, decoder_1_out0;
  wire [2:0] j_k_ff_1_q;

  Clock #(.highDuration(1), .lowDuration(1)) clock_1 (.out(clock_1_out));
  // Digital_Oscilloscope #(.nState(10), .frontlines("rising"), .showclock("true")) digital_oscilloscope_1: pin names not known; wires that end beside it: clock_1_out, out_1
  and and_1 (and_1_out, j_k_ff_1_q[1], j_k_ff_1_q[2]);
  J_K_Flip_Flop #(.trigger("rising"), .Pre_Clr_Positions("ABOVE_BELOW"), .NegatePresetClear("false"), .enable("false"), .NewFFLayout("true")) j_k_ff_1 (
    .J(and_1_out), .clk(clock_1_out), .K(and_1_out), .Q(j_k_ff_1_q[0]));  // open: Qn, preset, reset
  J_K_Flip_Flop #(.trigger("rising"), .Pre_Clr_Positions("ABOVE_BELOW"), .NegatePresetClear("false"), .enable("false"), .NewFFLayout("true")) j_k_ff_2 (
    .J(j_k_ff_1_q[2]), .clk(clock_1_out), .K(j_k_ff_1_q[2]), .Q(j_k_ff_1_q[1]));  // open: Qn, preset, reset
  J_K_Flip_Flop #(.trigger("rising"), .Pre_Clr_Positions("ABOVE_BELOW"), .NegatePresetClear("false"), .enable("false"), .NewFFLayout("true")) j_k_ff_3 (
    .J(1'b1), .clk(clock_1_out), .K(1'b1), .Q(j_k_ff_1_q[2]));  // open: Qn, preset, reset
  and and_2 (and_2_out, j_k_ff_1_q[0], j_k_ff_1_q[1], j_k_ff_1_q[2]);
  LED #(.active("true")) led_1 (.in(and_2_out));
  Decoder #(.select(3), .tristate("false"), .disabled("Z"), .enable("false")) decoder_1 (
    .out0(decoder_1_out0), .sel(j_k_ff_1_q));  // open: out1, out2, out3, out4, out5, out6, out7
  buf or_1 (out_1, decoder_1_out0);  // OR_Gate
endmodule
