// Logisim project 10进制.circ as structural Verilog: 1 circuit, main circuit main
module main (
  input  in_1
);

  wire and_1_out, and_2_out, and_3_out, and_4_out, clock_1_out, j_k_ff_1_q, j_k_ff_1_qn, j_k_ff_2_q,
       j_k_ff_3_q, j_k_ff_4_q;

  Clock #(.highDuration(1), .lowDuration(1)) clock_1 (.out(clock_1_out));
  and and_1 (and_1_out, j_k_ff_2_q, j_k_ff_4_q, j_k_ff_3_q);
  J_K_Flip_Flop #(.trigger("rising"), .Pre_Clr_Positions("ABOVE_BELOW"), .NegatePresetClear("false"), .enable("false"), .NewFFLayout("true")) j_k_ff_1 (
    .J(and_1_out), .clk(clock_1_out), .K(j_k_ff_4_q), .Q(j_k_ff_1_q), .Qn(j_k_ff_1_qn));  // open: preset, reset
  and and_2 (and_2_out, j_k_ff_4_q, j_k_ff_3_q);
  J_K_Flip_Flop #(.trigger("rising"), .Pre_Clr_Positions("ABOVE_BELOW"), .NegatePresetClear("false"), .enable("false"), .NewFFLayout("true")) j_k_ff_2 (
    .J(and_2_out), .clk(clock_1_out), .K(and_2_out), .Q(j_k_ff_2_q));  // open: Qn, preset, reset
  and and_3 (and_3_out, j_k_ff_1_q, j_k_ff_4_q);
  LED #(.active("true")) led_1 (.in(and_3_out));
  J_K_Flip_Flop #(.trigger("rising"), .Pre_Clr_Positions("ABOVE_BELOW"), .NegatePresetClear("false"), .enable("false"), .NewFFLayout("true")) j_k_ff_3 (
    .J(and_4_out), .clk(clock_1_out), .K(j_k_ff_4_q), .Q(j_k_ff_3_q));  // open: Qn, preset, reset
  and and_4 (and_4_out, j_k_ff_1_qn, j_k_ff_4_q);
  J_K_Flip_Flop #(.trigger("rising"), .Pre_Clr_Positions("ABOVE_BELOW"), .NegatePresetClear("false"), .enable("false"), .NewFFLayout("true")) j_k_ff_4 (
    .J(in_1), .clk(clock_1_out), .K(in_1), .Q(j_k_ff_4_q));  // open: Qn, preset, reset

  // Notes on the sheet:
  //   FF3
  //   FF2
  //   FF1
  //   FF0
endmodule
