// Logisim project 9进制.circ as structural Verilog: 1 circuit, main circuit main
module main (
  input  in_1
);

  wire and_1_out, and_2_out, and_3_out, and_4_out, and_5_out, and_6_out, and_7_out, clock_1_out, j_k_ff_1_q,
       j_k_ff_1_qn, j_k_ff_2_q, j_k_ff_3_q, j_k_ff_3_qn, j_k_ff_4_q, nand_1_out, or_1_out, or_2_out,
       or_3_out, or_4_out;

  Clock #(.highDuration(1), .lowDuration(1)) clock_1 (.out(clock_1_out));
  J_K_Flip_Flop #(.trigger("rising"), .Pre_Clr_Positions("ABOVE_BELOW"), .NegatePresetClear("false"), .enable("false"), .NewFFLayout("true")) j_k_ff_1 (
    .J(or_2_out), .clk(clock_1_out), .K(in_1), .Q(j_k_ff_1_q), .Qn(j_k_ff_1_qn));  // open: preset, reset
  and and_1 (and_1_out, j_k_ff_1_qn, j_k_ff_2_q, j_k_ff_3_q, j_k_ff_4_q);
  LED #(.active("true")) led_1 (.in(and_1_out));
  J_K_Flip_Flop #(.trigger("rising"), .Pre_Clr_Positions("ABOVE_BELOW"), .NegatePresetClear("false"), .enable("false"), .NewFFLayout("true")) j_k_ff_2 (
    .J(j_k_ff_1_q), .clk(clock_1_out), .K(and_7_out), .Q(j_k_ff_2_q));  // open: Qn, preset, reset
  and and_2 (and_2_out, j_k_ff_2_q, j_k_ff_3_q);
  or or_1 (or_1_out, j_k_ff_1_q, and_2_out);
  and and_3 (and_3_out, j_k_ff_1_q, j_k_ff_2_q);
  nand nand_1 (nand_1_out, j_k_ff_2_q, j_k_ff_4_q);
  J_K_Flip_Flop #(.trigger("rising"), .Pre_Clr_Positions("ABOVE_BELOW"), .NegatePresetClear("false"), .enable("false"), .NewFFLayout("true")) j_k_ff_3 (
    .J(and_3_out), .clk(clock_1_out), .K(and_4_out), .Q(j_k_ff_3_q), .Qn(j_k_ff_3_qn));  // open: preset, reset
  and and_4 (and_4_out, j_k_ff_2_q, j_k_ff_4_q);
  and and_5 (and_5_out, j_k_ff_3_qn, j_k_ff_4_q);
  or or_2 (or_2_out, nand_1_out, and_5_out);
  and and_6 (and_6_out, j_k_ff_1_q, j_k_ff_2_q, j_k_ff_3_q);
  J_K_Flip_Flop #(.trigger("rising"), .Pre_Clr_Positions("ABOVE_BELOW"), .NegatePresetClear("false"), .enable("false"), .NewFFLayout("true")) j_k_ff_4 (
    .J(and_6_out), .clk(clock_1_out), .K(or_1_out), .Q(j_k_ff_4_q));  // open: Qn, preset, reset
  and and_7 (and_7_out, or_4_out, or_3_out);
  or or_3 (or_3_out, j_k_ff_3_q, j_k_ff_1_q);
  or or_4 (or_4_out, j_k_ff_3_qn, j_k_ff_4_q);

  // Notes on the sheet:
  //   FF3
  //   FF2
  //   FF1
  //   FF0
endmodule
