// Logisim project Decorder38.circ as structural Verilog: 1 circuit, main circuit main
// Decorder38
module main (
  input  S3,
  input  S2,
  input  S1,
  input  A0,
  input  A1,
  input  A2,
  output Z0,
  output Z1,
  output Z2,
  output Z3,
  output Z4,
  output Z5,
  output Z6,
  output Z7
);

  wire and_1_out, not_1_out, not_2_out, not_3_out, not_4_out, not_5_out, not_6_out, not_7_out, not_8_out,
       not_9_out, not_10_out;

  not not_1 (not_1_out, S3);
  not not_2 (not_2_out, S2);
  not not_3 (not_3_out, S1);
  not not_4 (not_4_out, not_3_out);
  and and_1 (and_1_out, not_1_out, not_2_out, not_4_out);
  not not_5 (not_5_out, A0);
  not not_6 (not_6_out, A1);
  not not_7 (not_7_out, A2);
  not not_8 (not_8_out, not_5_out);
  not not_9 (not_9_out, not_6_out);
  not not_10 (not_10_out, not_7_out);
  nand nand_1 (Z0, not_5_out, not_6_out, not_7_out, and_1_out);
  nand nand_2 (Z1, not_8_out, not_6_out, not_7_out, and_1_out);
  nand nand_3 (Z2, not_5_out, not_9_out, not_7_out, and_1_out);
  nand nand_4 (Z3, not_8_out, not_9_out, not_7_out, and_1_out);
  nand nand_5 (Z4, not_5_out, not_6_out, not_10_out, and_1_out);
  nand nand_6 (Z5, not_6_out, not_10_out, not_8_out, and_1_out);
  nand nand_7 (Z6, not_5_out, not_10_out, not_9_out, and_1_out);
  nand nand_8 (Z7, and_1_out, not_9_out, not_8_out, not_10_out);
endmodule
