// Logisim project FullAdder_Decorder.circ as structural Verilog: 1 circuit, main circuit main
module main (
  input  in_1,
  input  in_2,
  input  in_3,
  output S,
  output CO
);

  wire main_1_z1, main_1_z2, main_1_z3, main_1_z4, main_1_z5, main_1_z6, main_1_z7;

  Decorder38_main main_1 (
    .S3(1'b0), .S2(1'b0), .S1(1'b1), .A0(in_1), .A1(in_2), .A2(in_3), .Z1(main_1_z1), .Z2(main_1_z2),
    .Z3(main_1_z3), .Z4(main_1_z4), .Z5(main_1_z5), .Z6(main_1_z6), .Z7(main_1_z7));  // open: Z0
  nand nand_1 (S, main_1_z1, main_1_z2, main_1_z4, main_1_z7);
  nand nand_2 (CO, main_1_z5, main_1_z6, main_1_z7, main_1_z3);
endmodule
