// Logisim project xxxxx.circ as structural Verilog: 1 circuit, main circuit main
module main (
  input  A,
  input  Ci,
  input  B,
  input  in_4,
  input  in_5,
  output S,
  output CO
);

  wire not_1_out;

  not not_1 (not_1_out, Ci);
  Multiplexer #(.select(2), .width(1), .disabled("Z"), .enable("false")) multiplexer_1 (
    .in0(Ci), .in1(not_1_out), .in2(not_1_out), .in3(Ci), .out(S), .sel({B, A}));
  Multiplexer #(.select(2), .width(1), .disabled("Z"), .enable("false")) multiplexer_2 (
    .in0(in_4), .in1(Ci), .in2(Ci), .in3(in_5), .out(CO), .sel({B, A}));
endmodule
