// Logisim project 全加器.circ as structural Verilog: 1 circuit, main circuit main
module main (
  input  A,
  input  B,
  input  C,
  output S,
  output CO
);

  wire and_1_out, and_2_out, and_3_out, not_1_out, not_2_out;

  not not_1 (not_1_out, B);
  not not_2 (not_2_out, C);
  xor xor_1 (S, A, B, C);
  and and_1 (and_1_out, A, not_1_out, C);
  and and_2 (and_2_out, A, B, not_2_out);
  and and_3 (and_3_out, B, C);
  or or_1 (CO, and_1_out, and_2_out, and_3_out);
endmodule
