// Logisim project 八选一.circ as structural Verilog: 1 circuit, main circuit main
module main (
  input  in_1,
  input  in_2,
  input  in_3,
  input  in_4,
  input  in_5,
  input  in_6,
  input  in_7,
  input  A,
  input  in_9,
  input  B,
  input  C,
  input  in_12,
  input  in_13,
  input  in_14,
  input  in_15,
  input  in_16,
  input  in_17,
  input  in_18,
  input  in_19,
  output S,
  output CO
);

  Multiplexer #(.select(3), .width(1), .disabled("Z"), .enable("false")) multiplexer_1 (
    .in0(in_3), .in1(in_2), .in2(in_1), .in3(in_4), .in4(in_6), .in5(in_7), .in6(in_5), .in7(in_9), .out(S),
    .sel({C, B, A}));
  Multiplexer #(.select(3), .width(1), .disabled("Z"), .enable("false")) multiplexer_2 (
    .in0(in_14), .in1(in_13), .in2(in_12), .in3(in_15), .in4(in_16), .in5(in_17), .in6(in_18), .in7(in_19),
    .out(CO), .sel({C, B, A}));
endmodule
